# Fritzing sketch Potentiometer7SegmentUno12V (saved by Fritzing 0.9.2b)

parts:
  Part3 = Arduino Uno (Rev3) - ICSP
  U1 = POT [package=pot_alpha_rv16af-20]
  PART1 = OpenSegment Serial Display - 20mm (Blue) [part_number=COM-11647]
  12V = Power plug

nets:
  N1: Part3.A0, U1.S
  N2: Part3.D10_PWM/SS, PART1.SS
  N3: Part3.D11_PWM/MOSI, PART1.SDI
  N4: Part3.D12/MISO, PART1.SDO
  N5: Part3.D13/SCK, PART1.SCK
  GND: Part3.GND, U1.E, PART1.GND, 12V.GND
  5V: Part3.5V, U1.A, PART1.VCC, PART1.+
  VIN: Part3.VIN, 12V.VCC

custom parts:
  OpenSegment Serial Display - 20mm (Blue): OpenSegment makes it easy to add a large 7-segment display to your project. Because larger 7-segment displays pull more power than a microcontroller is able to drive directly, the OpenSegment has 8 PNP and 4 NPN transistors in order to drive the segments at their maximum brightness! The on-board ATmega328 receives data over multiple digital interfaces (such as TWI, UART and SPI) and does all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
