# Fritzing sketch PotentiometerServoUno9V (saved by Fritzing 0.9.2b)

parts:
  J1 = Basic Servo
  Part3 = Arduino Uno (Rev3) - ICSP
  part = Battery block 9V
  U1 = POT [package=pot_alpha_rv16af-20]

nets:
  GND: J1.gnd, Part3.GND, part.-, U1.E
  VCC: J1.vcc, Part3.5V, U1.A
  N1: J1.pulse, Part3.D3_PWM
  N2: Part3.A0, U1.S
  N3: Part3.VIN, part.+
